# Fritzing sketch wiiproject (saved by Fritzing 0.9.2b)
breadboards: 1

parts:
  Raspberry_Pi_B_rev1 = Raspberry Pi B rev1
  U1 = 74HC595 [package="DIP16 [THT]"]
  U2 = 74HC595 [package="DIP16 [THT]"]
  R1 = Resistor [tolerance=±5% resistance=330 package=THT]
  R2 = Resistor [tolerance=±5% resistance=330 package=THT]
  R3 = Resistor [tolerance=±5% resistance=330 package=THT]
  R4 = Resistor [tolerance=±5% resistance=330 package=THT]
  R5 = Resistor [tolerance=±5% resistance=330 package=THT]
  R6 = Resistor [tolerance=±5% resistance=330 package=THT]
  R7 = Resistor [tolerance=±5% resistance=330 package=THT]
  R8 = Resistor [tolerance=±5% resistance=330 package=THT]
  Disp2 = LBT2088AH [part_number=LBT2088AH]

nets:
  N1: Raspberry_Pi_B_rev1.GND, U1.OE
  N2: Raspberry_Pi_B_rev1.GPIO_23, U2.SH_CP
  N3: Raspberry_Pi_B_rev1.GPIO_17, U1.DS
  N4: Raspberry_Pi_B_rev1.GPIO_18, U2.DS
  N5: Raspberry_Pi_B_rev1.GPIO_21, U1.SH_CP
  N6: Raspberry_Pi_B_rev1.GPIO_22, U1.ST_CP
  N7: Raspberry_Pi_B_rev1.GPIO_4, U1.MR
  N8: Raspberry_Pi_B_rev1.GPIO_24, U2.ST_CP
  N9: U1.Q1, Disp2.pin_14
  N10: U1.Q2, Disp2.pin_8
  N11: U1.Q3, Disp2.pin_12
  N12: U1.Q4, Disp2.pin1
  N13: U1.Q5, Disp2.pin_7
  N14: U1.Q6, Disp2.pin2
  N15: U1.Q7, Disp2.pin_5
  N16: U1.Q0, Disp2.pin_9
  N17: U2.Q1, R4.Pin_1
  N18: U2.Q2, R3.Pin_1
  N19: U2.Q3, R2.Pin_1
  N20: U2.Q4, R7.Pin_1
  N21: U2.Q5, R6.Pin_1
  N22: U2.Q6, R8.Pin_1
  N23: U2.Q7, R5.Pin_1
  N24: U2.Q0, R1.Pin_1
  N25: R1.Pin_0, Disp2.pin_16
  N26: R2.Pin_0, Disp2.pin_6
  N27: R3.Pin_0, Disp2.pin_11
  N28: R4.Pin_0, Disp2.pin_15
  N29: R5.Pin_0, Disp2.pin_13
  N30: R6.Pin_0, Disp2.pin_4
  N31: R7.Pin_0, Disp2.pin_10
  N32: R8.Pin_0, Disp2.pin_3
